# Fritzing sketch RGB_step (saved by Fritzing 0.9.3b)
circuit board: 8.46667cm x 5.64444cm
breadboards: 1

parts:
  Componente1 = Arduino Mega 2560 (Rev3)
  R1 = Resistor [tolerance=±5% resistance=220 package=THT]
  LED1 = RGB LED (com. cathode, rgb) [package="5 mm [THT]"]
  R2 = Resistor [tolerance=±5% resistance=220 package=THT]
  R3 = Resistor [tolerance=±5% resistance=220 package=THT]

nets:
  N1: Componente1.GND, LED1.common_cathode
  N2: Componente1.D3_PWM, R3.Pin_0
  N3: Componente1.D5_PWM, R2.Pin_0
  N4: Componente1.D6_PWM, R1.Pin_0
  N5: R1.Pin_1, LED1.red_anode
  N6: LED1.green_anode, R2.Pin_1
  N7: LED1.blue_anode, R3.Pin_1

// code stored in the sketch: RGB.ino
// MAINTAINER keopx <keopx@keopx.net>
// LICENSE GPLv3

// Define Pins
#define BLUE 3
#define GREEN 5
#define RED 6

void setup()
{
  pinMode(RED, OUTPUT);
  pinMode(GREEN, OUTPUT);
  pinMode(BLUE, OUTPUT);
  digitalWrite(RED, HIGH);
  digitalWrite(GREEN, LOW);
  digitalWrite(BLUE, LOW);
}

// define variables
int redValue;
int greenValue;
int blueValue;

// main loop
void loop()
{
  #define delayTime 10 // fading time between colors

  redValue = 255; // choose a value between 1 and 255 to change the color.
  greenValue = 0;
  blueValue = 0;

  // this is unnecessary as we've either turned on RED in SETUP
  // or in the previous loop ... regardless, this turns RED off
  // analogWrite(RED, 0);
  // delay(1000);

  for(int i = 0; i < 255; i += 1) // fades out red bring green full when i=255
  {
    redValue -= 1;
    greenValue += 1;
    // The following was reversed, counting in the wrong directions
    // analogWrite(RED, 255 - redValue);
    // analogWrite(GREEN, 255 - greenValue);
    analogWrite(RED, redValue);
    analogWrite(GREEN, greenValue);
    delay(delayTime);
  }

  redValue = 0;
  greenValue = 255;
  blueValue = 0;

  for(int i = 0; i < 255; i += 1) // fades out green bring blue full when i=255
  {
  	greenValue -= 1;
  	blueValue += 1;
  	// The following was reversed, counting in the wrong directions
  	// analogWrite(GREEN, 255 - greenValue);
  	// analogWrite(BLUE, 255 - blueValue);
  	analogWrite(GREEN, greenValue);
  	analogWrite(BLUE, blueValue);
  	delay(delayTime);
  }

  redValue = 0;
  greenValue = 0;
  blueValue = 255;

  for(int i = 0; i < 255; i += 1) // fades out blue bring red full when i=255
  {
  	// The following code has been rearranged to match the other two similar sections
  	blueValue -= 1;
  	redValue += 1;
  	// The following was reversed, counting in the wrong directions
  	// analogWrite(BLUE, 255 - blueValue);
  	// analogWrite(RED, 255 - redValue);
  	analogWrite(BLUE, blueValue);
  	analogWrite(RED, redValue);
  	delay(delayTime);
	}
}

// code stored in the sketch: RGB_step.ino
// MAINTAINER keopx <keopx@keopx.net>
// LICENSE GPLv3

// Define Pins
#define BLUE 3
#define GREEN 5
#define RED 6

// Delay time in milliseconds.
#define delayTime 1000 

// LED color intensity.
#define MIN 0 
#define MAX 255

void setup()
{
  pinMode(RED, OUTPUT);
  pinMode(GREEN, OUTPUT);
  pinMode(BLUE, OUTPUT);
  digitalWrite(RED, HIGH);
  digitalWrite(GREEN, LOW);
  digitalWrite(BLUE, LOW);
}

void red()
{
  analogWrite(RED, MAX);
  analogWrite(BLUE, MIN);
  analogWrite(GREEN, MIN);
}

void orange()
{
  analogWrite(RED, MAX);
  analogWrite(BLUE, MIN);
  analogWrite(GREEN, 50);
}

void blue()
{
  analogWrite(RED, MIN);
  analogWrite(BLUE, MAX);
  analogWrite(GREEN, MIN);
}

void green()
{
  analogWrite(RED, MIN);
  analogWrite(BLUE, MIN);
  analogWrite(GREEN, MAX);
}

// main loop
void loop()
{

  red();
  delay(delayTime);

  orange();
  delay(delayTime);

  blue();
  delay(delayTime);

  green();
  delay(delayTime);
}
