# Fritzing sketch Train_Barrier_Semaphore (saved by Fritzing 0.9.3b)

parts:
  hc-sr1 = hc-sr04
  LED1 = RGB LED (com. anode, rbg) [package="5 mm [THT]"]
  J1 = Basic Servo
  Componente1 = Arduino Uno (Rev3)

nets:
  VCC: hc-sr1.VCC, Componente1.5V
  N1: hc-sr1.Trig, Componente1.D6_PWM
  N2: hc-sr1.Echo, Componente1.D7
  GND: hc-sr1.GND, LED1.common_anode, J1.gnd, Componente1.GND
  N3: LED1.red_cathode, Componente1.D11_PWM/MOSI
  N4: LED1.blue_cathode, Componente1.D12/MISO
  N5: LED1.green_cathode, Componente1.D13/SCK
  N6: J1.vcc, Componente1.ioref
  N7: J1.pulse, Componente1.D9_PWM

// code stored in the sketch: RGB.ino
// MAINTAINER keopx <keopx@keopx.net>
// LICENSE GPLv3

// Define Pins
#define BLUE 3
#define GREEN 5
#define RED 6

void setup()
{
  pinMode(RED, OUTPUT);
  pinMode(GREEN, OUTPUT);
  pinMode(BLUE, OUTPUT);
  digitalWrite(RED, HIGH);
  digitalWrite(GREEN, LOW);
  digitalWrite(BLUE, LOW);
}

// define variables
int redValue;
int greenValue;
int blueValue;

// main loop
void loop()
{
  #define delayTime 10 // fading time between colors

  redValue = 255; // choose a value between 1 and 255 to change the color.
  greenValue = 0;
  blueValue = 0;

  // this is unnecessary as we've either turned on RED in SETUP
  // or in the previous loop ... regardless, this turns RED off
  // analogWrite(RED, 0);
  // delay(1000);

  for(int i = 0; i < 255; i += 1) // fades out red bring green full when i=255
  {
    redValue -= 1;
    greenValue += 1;
    // The following was reversed, counting in the wrong directions
    // analogWrite(RED, 255 - redValue);
    // analogWrite(GREEN, 255 - greenValue);
    analogWrite(RED, redValue);
    analogWrite(GREEN, greenValue);
    delay(delayTime);
  }

  redValue = 0;
  greenValue = 255;
  blueValue = 0;

  for(int i = 0; i < 255; i += 1) // fades out green bring blue full when i=255
  {
  	greenValue -= 1;
  	blueValue += 1;
  	// The following was reversed, counting in the wrong directions
  	// analogWrite(GREEN, 255 - greenValue);
  	// analogWrite(BLUE, 255 - blueValue);
  	analogWrite(GREEN, greenValue);
  	analogWrite(BLUE, blueValue);
  	delay(delayTime);
  }

  redValue = 0;
  greenValue = 0;
  blueValue = 255;

  for(int i = 0; i < 255; i += 1) // fades out blue bring red full when i=255
  {
  	// The following code has been rearranged to match the other two similar sections
  	blueValue -= 1;
  	redValue += 1;
  	// The following was reversed, counting in the wrong directions
  	// analogWrite(BLUE, 255 - blueValue);
  	// analogWrite(RED, 255 - redValue);
  	analogWrite(BLUE, blueValue);
  	analogWrite(RED, redValue);
  	delay(delayTime);
	}
}

// code stored in the sketch: RGB_Proximity.ino
// MAINTAINER keopx <keopx@keopx.net>
// LICENSE GPLv3

// Define Proximity Pins
#include "SR04.h"
#define TRIG_PIN 12
#define ECHO_PIN 11
SR04 sr04 = SR04(ECHO_PIN,TRIG_PIN);
long a;

// Define LED Pins
#define BLUE 3
#define GREEN 5
#define RED 6

// LED color intensity.
#define MIN 0
#define MAX 255

void setup()
{
  // LED.
  pinMode(RED, OUTPUT);
  pinMode(GREEN, OUTPUT);
  pinMode(BLUE, OUTPUT);
  digitalWrite(RED, HIGH);
  digitalWrite(GREEN, LOW);
  digitalWrite(BLUE, LOW);

  // Proximity.
  Serial.begin(9600);
  delay(1000);
}

void red()
{
  analogWrite(RED, MAX);
  analogWrite(BLUE, MIN);
  analogWrite(GREEN, MIN);
}

void orange()
{
  analogWrite(RED, MAX);
  analogWrite(BLUE, MIN);
  analogWrite(GREEN, 50);
}

void blue()
{
  analogWrite(RED, MIN);
  analogWrite(BLUE, MAX);
  analogWrite(GREEN, MIN);
}

void green()
{
  analogWrite(RED, MIN);
  analogWrite(BLUE, MIN);
  analogWrite(GREEN, MAX);
}

// main loop
void loop()
{

  a = sr04.Distance();
  Serial.print(a);
  Serial.println("cm");

  // Block.
  if (a > 5) {
    red();
  }

  // Access.
  if (a < 5) {
    orange();
    delay(2000);
    green();
    delay(2000);
  }
  // Delay time in milliseconds.
  delay(1000);
}

// code stored in the sketch: RGB_Proximity_Servo.ino
// MAINTAINER keopx <keopx@keopx.net>
// LICENSE GPLv3

// Define Servo.
#include <Servo.h>
Servo myservo;  // create servo object to control a servo
// twelve servo objects can be created on most boards
#define SERVO_PIN 9

int pos = 0;    // variable to store the servo position

// Define Proximity Pins
#include "SR04.h"
#define TRIG_PIN 12
#define ECHO_PIN 11
SR04 sr04 = SR04(ECHO_PIN, TRIG_PIN);
long distance;

// Define LED Pins
#define BLUE 3
#define GREEN 5
#define RED 6

// LED color intensity.
#define MIN 0
#define MAX 255

void setup()
{
  // LED.
  pinMode(RED, OUTPUT);
  pinMode(GREEN, OUTPUT);
  pinMode(BLUE, OUTPUT);
  digitalWrite(RED, HIGH);
  digitalWrite(GREEN, LOW);
  digitalWrite(BLUE, LOW);

  // Proximity.
  Serial.begin(9600);
  delay(1000);

  int pos = 0;
  myservo.attach(SERVO_PIN);  // attaches the servo on pin 9 to the servo object
}

void red()
{
  analogWrite(RED, MAX);
  analogWrite(BLUE, MIN);
  analogWrite(GREEN, MIN);
}

void orange()
{
  analogWrite(RED, MAX);
  analogWrite(BLUE, MIN);
  analogWrite(GREEN, 50);
}

void blue()
{
  analogWrite(RED, MIN);
  analogWrite(BLUE, MAX);
  analogWrite(GREEN, MIN);
}

void green()
{
  analogWrite(RED, MIN);
  analogWrite(BLUE, MIN);
  analogWrite(GREEN, MAX);
}

int openServo() {
  Serial.print("Open start: ");
  Serial.println(pos);
  for (pos = 0; pos < 90; pos += 1) { // goes from 0 degrees to 180 degrees
    // in steps of 1 degree
    myservo.write(pos);              // tell servo to go to position in variable 'pos'
    delay(15);                       // waits 15ms for the servo to reach the position
  }
}

int closeServo() {
  Serial.print("Close start: ");
  Serial.println(pos);
  for (pos = 90; pos >= 1; pos -= 1) { // goes from 0 degrees to 180 degrees
    // in steps of 1 degree
    myservo.write(pos);              // tell servo to go to position in variable 'pos'
    delay(15);                       // waits 15ms for the servo to reach the position
  }
  myservo.write(0);              // tell servo to go to position in variable 'pos'
  delay(15);                       // waits 15ms for the servo to reach the position
}

// main loop
void loop()
{
  distance = sr04.Distance();
  Serial.print(distance);
  Serial.println(" cm");

  Serial.print("Position: ");
  Serial.println(pos);

  // Block.
  if (distance > 10 && pos <= 0) {
    red();
  }

  // Warning and open.
  if (distance <= 10 && pos <= 0) {
    orange();
    openServo();
  }

  // Warning and Close.
  if (distance > 10 && pos >= 90) {
    orange();
    delay(2000);
    closeServo();
  }

  // Access granted and opened.
  if (distance <= 10 && pos >= 90) {
    green();
  }

  delay(1000);
}

// code stored in the sketch: RGB_step.ino
// MAINTAINER keopx <keopx@keopx.net>
// LICENSE GPLv3

// Define Pins
#define BLUE 3
#define GREEN 5
#define RED 6

// Delay time in milliseconds.
#define delayTime 1000 

// LED color intensity.
#define MIN 0 
#define MAX 255

void setup()
{
  pinMode(RED, OUTPUT);
  pinMode(GREEN, OUTPUT);
  pinMode(BLUE, OUTPUT);
  digitalWrite(RED, HIGH);
  digitalWrite(GREEN, LOW);
  digitalWrite(BLUE, LOW);
}

void red()
{
  analogWrite(RED, MAX);
  analogWrite(BLUE, MIN);
  analogWrite(GREEN, MIN);
}

void orange()
{
  analogWrite(RED, MAX);
  analogWrite(BLUE, MIN);
  analogWrite(GREEN, 50);
}

void blue()
{
  analogWrite(RED, MIN);
  analogWrite(BLUE, MAX);
  analogWrite(GREEN, MIN);
}

void green()
{
  analogWrite(RED, MIN);
  analogWrite(BLUE, MIN);
  analogWrite(GREEN, MAX);
}

// main loop
void loop()
{

  red();
  delay(delayTime);

  orange();
  delay(delayTime);

  blue();
  delay(delayTime);

  green();
  delay(delayTime);
}

// code stored in the sketch: Train_Barrier.ino
// MAINTAINER keopx <keopx@keopx.net>
// LICENSE GPLv3

// Define Servo.
#include <Servo.h>
Servo myservo;  // create servo object to control a servo
// twelve servo objects can be created on most boards
#define SERVO_PIN 9

int pos = 0;    // variable to store the servo position

// Define Proximity Pins
#include "SR04.h"
#define TRIG_PIN 12
#define ECHO_PIN 11
SR04 sr04 = SR04(ECHO_PIN, TRIG_PIN);
long distance;

// Define LED Pins
#define BLUE 3
#define GREEN 5
#define RED 6

// LED color intensity.
#define MIN 0
#define MAX 255

void setup()
{
  // LED.
  pinMode(RED, OUTPUT);
  pinMode(GREEN, OUTPUT);
  pinMode(BLUE, OUTPUT);
  digitalWrite(RED, HIGH);
  digitalWrite(GREEN, LOW);
  digitalWrite(BLUE, LOW);

  // Proximity.
  Serial.begin(9600);
  delay(1000);

  int pos = 0;
  myservo.attach(SERVO_PIN);  // attaches the servo on pin 9 to the servo object
}

void red()
{
  analogWrite(RED, MAX);
  analogWrite(BLUE, MIN);
  analogWrite(GREEN, MIN);
}

void orange()
{
  analogWrite(RED, MAX);
  analogWrite(BLUE, MIN);
  analogWrite(GREEN, 50);
}

void blue()
{
  analogWrite(RED, MIN);
  analogWrite(BLUE, MAX);
  analogWrite(GREEN, MIN);
}

void green()
{
  analogWrite(RED, MIN);
  analogWrite(BLUE, MIN);
  analogWrite(GREEN, MAX);
}

int openServo() {
  Serial.print("Open start: ");
  Serial.println(pos);
  for (pos = 0; pos < 90; pos += 1) { // goes from 0 degrees to 180 degrees
    // in steps of 1 degree
    myservo.write(pos);              // tell servo to go to position in variable 'pos'
    delay(15);                       // waits 15ms for the servo to reach the position
  }
}

int closeServo() {
  Serial.print("Close start: ");
  Serial.println(pos);
  for (pos = 90; pos >= 1; pos -= 1) { // goes from 0 degrees to 180 degrees
    // in steps of 1 degree
    myservo.write(pos);              // tell servo to go to position in variable 'pos'
    delay(15);                       // waits 15ms for the servo to reach the position
  }
  myservo.write(0);              // tell servo to go to position in variable 'pos'
  delay(15);                       // waits 15ms for the servo to reach the position
}

// main loop
void loop()
{
  distance = sr04.Distance();
  Serial.print(distance);
  Serial.println(" cm");

  Serial.print("Position: ");
  Serial.println(pos);

  // Block.
  if (distance > 10 && pos <= 0) {
    red();
  }

  // Warning and open.
  if (distance <= 10 && pos <= 0) {
    orange();
    openServo();
  }

  // Warning and Close.
  if (distance > 10 && pos >= 90) {
    orange();
    delay(2000);
    closeServo();
  }

  // Access granted and opened.
  if (distance <= 10 && pos >= 90) {
    green();
  }

  delay(1000);
}

// code stored in the sketch: Train_Barrier_Semaphore.ino
// MAINTAINER keopx <keopx@keopx.net>
// LICENSE GPLv3

// Define Servo.
#include <Servo.h>
Servo myservo;  // create servo object to control a servo
#define SERVO_PIN 9
int pos = 0;    // variable to store the servo position

// Define Proximity Pins
#include "SR04.h"
#define TRIG_PIN 6
#define ECHO_PIN 7
SR04 sr04 = SR04(ECHO_PIN, TRIG_PIN);
long distance;

// Define LED Pins
#define RED    11
#define YELLOW 12
#define GREEN  13

// LED color intensity.
#define MIN 0
#define MAX 255

// Barrier status
#define OPEN 0
#define CLOSE 90

// Distance
#define DISTANCE 10

void setup()
{
  // LED.
  pinMode(RED, OUTPUT);
  pinMode(GREEN, OUTPUT);
  pinMode(YELLOW, OUTPUT);
  digitalWrite(RED, HIGH);
  digitalWrite(GREEN, LOW);
  digitalWrite(YELLOW, LOW);

  // Proximity.
  Serial.begin(9600);
  delay(1000);

  int pos = CLOSE;
  myservo.attach(SERVO_PIN);  // attaches the servo on pin 9 to the servo object
}

void red()
{
  analogWrite(RED, MAX);
  analogWrite(YELLOW, MIN);
  analogWrite(GREEN, MIN);
}

void yellow()
{
  analogWrite(RED, MIN);
  analogWrite(YELLOW, MAX);
  analogWrite(GREEN, MIN);
}

void green()
{
  analogWrite(RED, MIN);
  analogWrite(YELLOW, MIN);
  analogWrite(GREEN, MAX);
}

int closeServo() {
  Serial.print("Close start: ");
  Serial.println(pos);
  for (pos = OPEN; pos < CLOSE; pos += 1) { // goes from 0 degrees to 180 degrees
    // in steps of 1 degree
    myservo.write(pos);              // tell servo to go to position in variable 'pos'
    delay(15);                       // waits 15ms for the servo to reach the position
  }
}

int openServo() {
  Serial.print("Open start: ");
  Serial.println(pos);
  int pos_new = OPEN + 1;
  for (pos = CLOSE; pos >= pos_new; pos -= 1) { // goes from 0 degrees to 180 degrees
    // in steps of 1 degree
    myservo.write(pos);              // tell servo to go to position in variable 'pos'
    delay(15);                       // waits 15ms for the servo to reach the position
  }
  myservo.write(0);              // tell servo to go to position in variable 'pos'
  delay(15);                       // waits 15ms for the servo to reach the position
}

// main loop
void loop()
{
  distance = sr04.Distance();
  Serial.print(distance);
  Serial.println(" cm");

  Serial.print("Position: ");
  Serial.println(pos);

  // Close.
  if (distance > DISTANCE && pos >= CLOSE) {
    red();
  }

  // Warning and open.
  if (distance <= DISTANCE && pos >= CLOSE) {
    yellow();
    openServo();
  }

  // Warning and Close.
  if (distance > DISTANCE && pos <= OPEN) {
    yellow();
    delay(2000);
    closeServo();
  }

  // Access granted and opened.
  if (distance <= DISTANCE && pos <= OPEN) {
    green();
  }

  delay(1000);
}
